# Fritzing sketch exquema (saved by Fritzing 1.0.5)
breadboards: 1

parts:
  WeMos_D1_Mini1 = WeMos D1 Mini
  U1 = 2-Channel 5v Relay Shield [package=relay-2ch5v10a]
  LED1 = LEDs [package=led10mm]
  LED2 = LEDs [package=led10mm]
  J2 = Camdenboss CTB0158-2 [part_number=CTB0158-2 package=THT]

nets:
  N1: WeMos_D1_Mini1.G, U1.GND
  N2: U1.K1-In, U1.K2-In, J2.terminal_2
  N3: U1.K1-Off, LED1.A
  N4: U1.K2-Off, LED2.A
  N5: LED1.C, LED2.C, J2.terminal_1

custom parts:
  2-Channel 5v Relay Shield: 2 Channel 5v Relay Shield w. 2x SPD-06VDC-SD-C
  LEDs: LEDs Standard schematic elements and footprints for 5mm, 3mm, 1206, and 0603 sized LEDs. 5mm - Spark Fun Electronics SKU : COM-00529 (and others)
